// Logisim project Indirect_Adressing_Unit.circ as structural Verilog: 1 circuit, main circuit Indirect_Adressing_Unit
module Indirect_Adressing_Unit (
  input  RESET,
  input  CLK,
  input  [15:0] DATA_0,
  input  [15:0] DATA_1,
  input  [15:0] DATA_2,
  input  in_6,
  output [15:0] OUTPUT_0,
  output [15:0] OUTPUT_1,
  output [15:0] OUTPUT_2,
  output [15:0] REG_ADRESS,
  output [15:0] RAM_ADRESS
);

  wire adress_comparator_4bit_1_output_adress, adress_comparator_4bit_2_output_adress,
       adress_comparator_4bit_3_output_adress, and_1_out, and_2_out, and_3_out, and_4_out, and_5_out,
       and_6_out, and_7_out, and_8_out, and_9_out, and_10_out, d_ff_1_q, d_ff_2_q, d_ff_3_q, d_ff_4_q,
       d_ff_4_qn, d_ff_5_q, d_ff_6_q, d_ff_6_qn, d_ff_7_q, d_ff_8_q, d_ff_8_qn, not_1_out, not_2_out,
       not_3_out, or_1_out, or_2_out, or_3_out, subtractor_1_bout;
  wire [3:0] multiplexer_1_out, multiplexer_2_out, multiplexer_3_out, register_4_q, register_5_q,
       register_6_q, subtractor_2_out, subtractor_3_out, subtractor_4_out;
  wire [4:0] register_1_q;
  wire [15:0] register_2_q, register_3_q;
  wire [15:5] register_1_q_2;

  and and_1 (and_1_out, RESET, CLK);
  D_Flip_Flop d_ff_1 (.D(1'b1), .clk(CLK), .Q(d_ff_1_q), .reset(and_1_out));  // open: Qn, preset
  Register #(.width(16)) register_1 (
    .D(DATA_0), .en(1'b1), .clk(d_ff_1_q), .Q({register_1_q_2, register_1_q}), .clr(and_1_out));
  Subtractor #(.width(5)) subtractor_1 (.a(register_1_q), .b(5'b10010), .bout(subtractor_1_bout));  // open: out, bin
  D_Flip_Flop d_ff_2 (.D(1'b1), .clk(CLK), .Q(d_ff_2_q), .reset(and_1_out));  // open: Qn, preset
  Register #(.width(16)) register_2 (.D(DATA_1), .en(1'b1), .clk(d_ff_2_q), .Q(register_2_q), .clr(and_1_out));
  D_Flip_Flop d_ff_3 (.D(1'b1), .clk(CLK), .Q(d_ff_3_q), .reset(and_1_out));  // open: Qn, preset
  Register #(.width(16)) register_3 (.D(DATA_2), .en(1'b1), .clk(d_ff_3_q), .Q(register_3_q), .clr(and_1_out));
  D_Flip_Flop d_ff_4 (.D(register_2_q[5]), .clk(CLK), .Q(d_ff_4_q), .Qn(d_ff_4_qn), .reset(and_1_out));  // open: preset
  and and_2 (and_2_out, not_1_out, in_6);
  or or_1 (or_1_out, and_2_out, d_ff_4_qn);
  not not_1 (not_1_out, adress_comparator_4bit_1_output_adress);
  Register #(.width(4)) register_4 (
    .D(multiplexer_1_out), .en(1'b1), .clk(and_3_out), .Q(register_4_q), .clr(and_1_out));
  Multiplexer #(.width(4)) multiplexer_1 (
    .in0(subtractor_2_out), .in1(4'b0100), .out(multiplexer_1_out), .sel(d_ff_4_qn));
  and and_3 (and_3_out, or_1_out, register_2_q[5], CLK);
  Subtractor #(.width(4)) subtractor_2 (.a(register_4_q), .b(4'b0001), .out(subtractor_2_out));  // open: bin, bout
  D_Flip_Flop d_ff_5 (.D(and_4_out), .clk(CLK), .Q(d_ff_5_q), .reset(and_1_out));  // open: Qn, preset
  and and_4 (and_4_out, d_ff_4_q, adress_comparator_4bit_1_output_adress);
  Adress_Comparator_4bit adress_comparator_4bit_1 (
    .ADRESS(register_4_q), .PHYSICAL_ADRESS(4'b0000), .OUTPUT_ADRESS(adress_comparator_4bit_1_output_adress));
  D_Flip_Flop d_ff_6 (.D(register_2_q[6]), .clk(CLK), .Q(d_ff_6_q), .Qn(d_ff_6_qn), .reset(and_1_out));  // open: preset
  and and_5 (and_5_out, not_2_out, d_ff_5_q);
  not not_2 (not_2_out, adress_comparator_4bit_2_output_adress);
  or or_2 (or_2_out, and_5_out, d_ff_6_qn);
  Subtractor #(.width(4)) subtractor_3 (.a(register_5_q), .b(4'b0001), .out(subtractor_3_out));  // open: bin, bout
  Register #(.width(4)) register_5 (
    .D(multiplexer_2_out), .en(1'b1), .clk(and_6_out), .Q(register_5_q), .clr(and_1_out));
  Multiplexer #(.width(4)) multiplexer_2 (
    .in0(subtractor_3_out), .in1(4'b0100), .out(multiplexer_2_out), .sel(d_ff_6_qn));
  and and_6 (and_6_out, or_2_out, register_2_q[6], CLK);
  and and_7 (and_7_out, d_ff_6_q, adress_comparator_4bit_2_output_adress);
  Adress_Comparator_4bit adress_comparator_4bit_2 (
    .ADRESS(register_5_q), .PHYSICAL_ADRESS(4'b0000), .OUTPUT_ADRESS(adress_comparator_4bit_2_output_adress));
  D_Flip_Flop d_ff_7 (.D(and_7_out), .clk(CLK), .Q(d_ff_7_q), .reset(and_1_out));  // open: Qn, preset
  D_Flip_Flop d_ff_8 (.D(register_2_q[7]), .clk(CLK), .Q(d_ff_8_q), .Qn(d_ff_8_qn), .reset(and_1_out));  // open: preset
  and and_8 (and_8_out, not_3_out, d_ff_7_q);
  or or_3 (or_3_out, and_8_out, d_ff_8_qn);
  not not_3 (not_3_out, adress_comparator_4bit_3_output_adress);
  Register #(.width(4)) register_6 (
    .D(multiplexer_3_out), .en(1'b1), .clk(and_9_out), .Q(register_6_q), .clr(and_1_out));
  Multiplexer #(.width(4)) multiplexer_3 (
    .in0(subtractor_4_out), .in1(4'b0100), .out(multiplexer_3_out), .sel(d_ff_8_qn));
  and and_9 (and_9_out, or_3_out, register_2_q[7], CLK);
  Subtractor #(.width(4)) subtractor_4 (.a(register_6_q), .b(4'b0001), .out(subtractor_4_out));  // open: bin, bout
  and and_10 (and_10_out, d_ff_8_q, adress_comparator_4bit_3_output_adress);
  Adress_Comparator_4bit adress_comparator_4bit_3 (
    .ADRESS(register_6_q), .PHYSICAL_ADRESS(4'b0000), .OUTPUT_ADRESS(adress_comparator_4bit_3_output_adress));
endmodule
